// Digital circuit cpu.dig as structural Verilog
module cpu (
  input  CLK
);

  wire notconnected_1_out, notconnected_2_out, notconnected_3_out;
  wire [15:0] notconnected_4_out, notconnected_5_out, notconnected_6_out;

  RAMDualAccess #(.AddrBits(16), .isProgramMemory("true"), .Bits(16)) RAM (
    .str(notconnected_1_out), .C(notconnected_2_out), .ld(notconnected_3_out), .A1(notconnected_4_out),
    .Din1(notconnected_5_out), .A2(notconnected_6_out));  // open: D1, D2
  // NotConnected on notconnected_1_out
  // NotConnected on notconnected_2_out
  // NotConnected on notconnected_3_out
  // NotConnected on notconnected_4_out
  // NotConnected on notconnected_5_out
  // NotConnected on notconnected_6_out
endmodule
